// Digital circuit 8bit_Register.dig as structural Verilog
module _8bit_Register (
  input  WE,
  input  [7:0] Din,
  output [7:0] Dout
);

  // Latch latch_1: pin names not known; wires that end beside it: Din[0], WE, Dout[0]
  // Latch latch_2: pin names not known; wires that end beside it: Din[1], WE, Dout[1]
  // Latch latch_3: pin names not known; wires that end beside it: Din[2], WE, Dout[2]
  // Latch latch_4: pin names not known; wires that end beside it: Din[3], WE, Dout[3]
  // Latch latch_5: pin names not known; wires that end beside it: Din[4], WE, Dout[4]
  // Latch latch_6: pin names not known; wires that end beside it: Din[5], WE, Dout[5]
  // Latch latch_7: pin names not known; wires that end beside it: Din[6], WE, Dout[6]
  // Latch latch_8: pin names not known; wires that end beside it: Din[7], WE, Dout[7]
endmodule
