// Digital circuit CPU_Memory.dig as structural Verilog
module CPU_Memory (
  input  WE,
  input  OE,
  input  WE_2,
  input  OE_2,
  input  WE_3,
  input  OE_3,
  input  OE_4,
  input  [7:0] Test,
  input  WE_4,
  input  WE_5,
  input  OE_5,
  input  WE_6,
  input  OE_6,
  input  WE_7,
  input  OE_7,
  input  WE_8,
  input  OE_8,
  output [7:0] RegA,
  output [7:0] RegB,
  output [7:0] ALU_Result,
  output Carry_Flag,
  output [7:0] Output_Reg,
  output [7:0] IR,
  output [3:0] MAR,
  output [7:0] MBR
);

  wire Clock;
  wire [3:0] _4bit_register_1_dout;
  wire [7:0] _8bit_adderalu_1_dout, _8bit_register_1_dout, _8bit_register_2_dout, _8bit_register_3_dout,
       Output_Reg_dout;

  Button u_Clock (.out(Clock));
  _8bit_Register _8bit_register_1 (
    .Din(Output_Reg_dout), .WE(WE_5), .OE(OE_5), .Clock(Clock), .Dout(_8bit_register_1_dout), .Stored_Data(IR));
  _8bit_Register _8bit_register_2 (
    .Din(Output_Reg_dout), .WE(WE), .OE(OE), .Clock(Clock), .Dout(_8bit_register_2_dout), .Stored_Data(RegA));
  _8bit_Register _8bit_register_3 (
    .Din(Output_Reg_dout), .WE(WE_2), .OE(OE_2), .Clock(Clock), .Dout(_8bit_register_3_dout),
    .Stored_Data(RegB));
  _8bit_AdderALU _8bit_adderalu_1 (
    .RegisterA(_8bit_register_2_dout), .RegisterB(_8bit_register_3_dout), .OE(OE_4),
    .Dout(_8bit_adderalu_1_dout), .ALU_Result(ALU_Result), .Carry_Flag(Carry_Flag));
  _4bit_Register _4bit_register_1 (
    .Din(_8bit_register_1_dout[3:0]), .WE(WE_6), .OE(OE_6), .Clock(Clock), .Dout(_4bit_register_1_dout),
    .Stored_Data(MAR));
  _8bit_Register u_Output_Reg (
    .Din(_8bit_adderalu_1_dout), .WE(WE_3), .OE(OE_3), .Clock(Clock), .Dout(Output_Reg_dout),
    .Stored_Data(Output_Reg));
  assign Output_Reg_dout = WE_4 ? Test : 8'bz;  // Driver driver_1
  _8bit_Register MBR_Memory_Buffer_Register (
    .Din(Output_Reg_dout), .WE(WE_7), .OE(OE_7), .Clock(Clock), .Dout(Output_Reg_dout), .Stored_Data(MBR));
  EEPROMDualPort #(.AddrBits(4), .Bits(8)) Memory (
    .A(_4bit_register_1_dout), .Din(Output_Reg_dout), .str(WE_8), .C(Clock), .ld(OE_8), .D(Output_Reg_dout));

  // Notes on the sheet:
  //   IR CPU Instruction Register
  //   RegA
  //   RegB
  //   CPU Internal Address Bus
  //   ALU
  //   MAR Memory Address Register
  //   CPU Internal data bus
  //   CPU External Address Bus
  //   CPU External data bus
  //   contents of Memory (hex, n*v repeats v):
  //   e,1f,20,3f,10*0,f,1
endmodule
