// Digital circuit 4bit_Register.dig as structural Verilog
module _4bit_Register (
  input  [3:0] Din,
  input  WE,
  input  OE,
  input  Clock,
  output [3:0] Dout,
  output [3:0] Stored_Data
);

  Register #(.Bits(4)) register_1 (.D(Din), .C(Clock), .en(WE), .Q(Stored_Data));
  assign Dout = OE ? Stored_Data : 4'bz;  // Driver driver_1
endmodule
