// Digital circuit 8bit_AdderALU.dig as structural Verilog
module _8bit_AdderALU (
  input  [7:0] RegisterA,
  input  [7:0] RegisterB,
  input  OE,
  output [7:0] Dout,
  output [7:0] ALU_Result,
  output Carry_Flag
);

  Add #(.Bits(8)) add_1 (.a(RegisterA), .b(RegisterB), .c_i(1'b0), .s(ALU_Result), .c_o(Carry_Flag));
  assign Dout = OE ? ALU_Result : 8'bz;  // Driver driver_1
  PullDown pulldown_1 (.out(Carry_Flag));
  PullDown #(.Bits(8)) pulldown_2 (.out(ALU_Result));
endmodule
