// Digital circuit 8bit_Register.dig as structural Verilog
module _8bit_Register (
  input  [7:0] Din,
  input  WE,
  input  OE,
  input  Clock,
  output [7:0] Dout,
  output [7:0] Stored_Data
);

  Register #(.Bits(8)) register_1 (.D(Din), .C(Clock), .en(WE), .Q(Stored_Data));
  assign Dout = OE ? Stored_Data : 8'bz;  // Driver driver_1
endmodule
