// Digital circuit Computer.dig as structural Verilog
module Computer (
  input  clk,
  output [7:0] RegA,
  output [7:0] RegB,
  output [7:0] ALU_Result,
  output Carry_Flag,
  output [7:0] Output_Reg,
  output [3:0] MAR,
  output [7:0] MBR,
  output Ovf,
  output [3:0] PC,
  output ovf_2,
  output [2:0] out_11,
  output [3:0] OPAddr,
  output [3:0] OPCode
);

  wire _0, _1, _2, _3, _4, _5, _6, _7, _8, _9, _10, _11, _12, _13, _14, _15, _16, button_1_out, Clock;
  wire [3:0] _4bit_register_1_dout, _8bit_register_1_stored_data;
  wire [7:0] _8bit_adderalu_1_dout, _8bit_register_2_dout, _8bit_register_3_dout, Output_Reg_dout;
  wire [7:4] _8bit_register_1_dout;

  Counter #(.Bits(3)) counter_1 (.en(1'b1), .C(Clock), .clr(1'b0), .out(out_11), .ovf(ovf_2));
  Switch switch_1 (.A(clk), .B(Clock));
  Button button_1 (.out(button_1_out));
  Switch switch_2 (.A(button_1_out), .B(Clock));
  LookUpTable #(.Bits(17)) u_OPCode (
    .in0(out_11[0]), .in1(out_11[1]), .in2(out_11[2]), .in3(OPCode[0]), .in4(OPCode[1]),
    .out({_16, _15, _14, _13, _12, _11, _10, _9, _8, _7, _6, _5, _4, _3, _2, _1, _0}));
  Counter #(.Bits(2)) u_PC (.en(_1), .C(Clock), .clr(1'b0), .out(PC[1:0]), .ovf(Ovf));
  _8bit_Register _8bit_register_1 (
    .Din(Output_Reg_dout), .WE(_2), .OE(_3), .Clock(Clock), .Dout({_8bit_register_1_dout, OPAddr}),
    .Stored_Data({OPCode, _8bit_register_1_stored_data}));
  _8bit_Register _8bit_register_2 (
    .Din(Output_Reg_dout), .WE(_4), .OE(_5), .Clock(Clock), .Dout(_8bit_register_2_dout), .Stored_Data(RegA));
  _8bit_Register _8bit_register_3 (
    .Din(Output_Reg_dout), .WE(_6), .OE(_7), .Clock(Clock), .Dout(_8bit_register_3_dout), .Stored_Data(RegB));
  assign OPAddr = _0 ? {2'b00, PC[1:0]} : 4'bz;  // Driver driver_1
  _8bit_AdderALU _8bit_adderalu_1 (
    .RegisterA(_8bit_register_2_dout), .RegisterB(_8bit_register_3_dout), .OE(_8),
    .Dout(_8bit_adderalu_1_dout), .ALU_Result(ALU_Result), .Carry_Flag(Carry_Flag));
  _4bit_Register _4bit_register_1 (
    .Din(OPAddr), .WE(_9), .OE(_10), .Clock(Clock), .Dout(_4bit_register_1_dout), .Stored_Data(MAR));
  _8bit_Register u_Output_Reg (
    .Din(_8bit_adderalu_1_dout), .WE(_11), .OE(_12), .Clock(Clock), .Dout(Output_Reg_dout),
    .Stored_Data(Output_Reg));
  _8bit_Register MBR_Memory_Buffer_Register (
    .Din(Output_Reg_dout), .WE(_15), .OE(_16), .Clock(Clock), .Dout(Output_Reg_dout), .Stored_Data(MBR));
  EEPROMDualPort #(.AddrBits(4), .Bits(8)) Memory (
    .A(_4bit_register_1_dout), .Din(Output_Reg_dout), .str(_13), .C(Clock), .ld(_14), .D(Output_Reg_dout));

  assign PC[3:2] = 2'b00;

  // Notes on the sheet:
  //   clk: Hz: 5
  //   2bit + 3bit
  //   contents of OPCode (hex, n*v repeats v):
  //   201,2,c400,10004,208,c400,10010,0,201,2,c400,10004,208,c400,10040
  //   ,0,201,2,c400,10004,9a0,0,0,0,201,2,c400,10004,9208,12400
  //   OE
  //   EN
  //   WE
  //   IR CPU Instruction Register
  //   RegA
  //   RegB
  //   CPU Internal Address Bus
  //   ALU
  //   MAR Memory Address Register
  //   CPU Internal data bus
  //   CPU External Address Bus
  //   CPU External data bus
  //   contents of Memory (hex, n*v repeats v):
  //   e,1f,20,3f,10*0,f,6a
endmodule
