// Digital circuit PC.dig as structural Verilog
module PC (
  input  EN,
  output [1:0] OUT,
  output Overflow_Flag
);

  wire button_1_out;

  Button button_1 (.out(button_1_out));
  Counter #(.Bits(2)) counter_1 (.en(EN), .C(button_1_out), .clr(1'b0), .out(OUT), .ovf(Overflow_Flag));
endmodule
