// Digital circuit EEPROM_SimpleUse.dig as structural Verilog
module EEPROM_SimpleUse (
  input  [7:0] Din,
  input  [3:0] ADDR,
  input  WE,
  input  OE,
  output [7:0] out_5
);

  wire Clock_out;

  Button Clock (.out(Clock_out));
  EEPROMDualPort #(.AddrBits(4), .Bits(8)) eepromdualport_1 (
    .A(ADDR), .Din(Din), .str(WE), .C(Clock_out), .ld(OE), .D(out_5));

  // Notes on the sheet:
  //   contents of eepromdualport_1 (hex, n*v repeats v):
  //   e,1f,20,3f,10*0,f,1
endmodule
