// Digital circuit Eight_bit_adder.dig as structural Verilog
module Eight_bit_adder (
  input  [7:0] A,
  input  [7:0] B,
  output [7:0] SUM,
  output OverflowFlag
);

  wire full_adder_1_carry, full_adder_2_carry, full_adder_3_carry, full_adder_4_carry, full_adder_5_carry,
       full_adder_6_carry, half_adder_1_carry;

  Half_Adder half_adder_1 (.A(A[0]), .B(B[0]), .SUM(SUM[0]), .Carry(half_adder_1_carry));
  Full_Adder full_adder_1 (
    .A(A[1]), .B(B[1]), .LastCarry(half_adder_1_carry), .SUM(SUM[1]), .Carry(full_adder_1_carry));
  Full_Adder full_adder_2 (
    .A(A[2]), .B(B[2]), .LastCarry(full_adder_1_carry), .SUM(SUM[2]), .Carry(full_adder_2_carry));
  Full_Adder full_adder_3 (
    .A(A[3]), .B(B[3]), .LastCarry(full_adder_2_carry), .SUM(SUM[3]), .Carry(full_adder_3_carry));
  Full_Adder full_adder_4 (
    .A(A[4]), .B(B[4]), .LastCarry(full_adder_3_carry), .SUM(SUM[4]), .Carry(full_adder_4_carry));
  Full_Adder full_adder_5 (
    .A(A[5]), .B(B[5]), .LastCarry(full_adder_4_carry), .SUM(SUM[5]), .Carry(full_adder_5_carry));
  Full_Adder full_adder_6 (
    .A(A[6]), .B(B[6]), .LastCarry(full_adder_5_carry), .SUM(SUM[6]), .Carry(full_adder_6_carry));
  Full_Adder full_adder_7 (.A(A[7]), .B(B[7]), .LastCarry(full_adder_6_carry), .SUM(SUM[7]), .Carry(OverflowFlag));
endmodule
