// Digital circuit Full_Adder.dig as structural Verilog
module Full_Adder (
  input  A,
  input  B,
  input  LastCarry,
  output SUM,
  output Carry
);

  wire half_adder_1_carry, half_adder_1_sum, half_adder_2_carry;

  Half_Adder half_adder_1 (.A(A), .B(B), .SUM(half_adder_1_sum), .Carry(half_adder_1_carry));
  Half_Adder half_adder_2 (.A(LastCarry), .B(half_adder_1_sum), .SUM(SUM), .Carry(half_adder_2_carry));
  or or_1 (Carry, half_adder_2_carry, half_adder_1_carry);
endmodule
