// Digital circuit Latch-Memory.dig as structural Verilog
module Latch_Memory (
  input  Din,
  input  WE,
  output Out
);

  wire and_1_out, and_2_out, not_1_out, not_2_out, or_1_out;

  not not_1 (not_1_out, Din);
  and and_1 (and_1_out, Din, WE);
  and and_2 (and_2_out, not_1_out, WE);
  or or_1 (or_1_out, Out, and_1_out);
  not not_2 (not_2_out, and_2_out);
  and and_3 (Out, or_1_out, not_2_out);

  // Notes on the sheet:
  //   Din: Data input
  //   WE: Write Enable
endmodule
