// Digital circuit Memory.dig as structural Verilog
module Memory (
  input  Din,
  input  ld,
  input  str,
  input  [3:0] Address_Number,
  output Dout
);

  wire [7:0] lookuptable_1_out;

  LookUpTable #(.Bits(8)) lookuptable_1 (
    .in0(Address_Number[0]), .in1(Address_Number[1]), .in2(Address_Number[2]), .in3(Address_Number[3]),
    .out(lookuptable_1_out));
  Memory_Cell memory_cell_1 (
    .ld(ld), .Din(Din), .str(str), .row(lookuptable_1_out[0]), .column(lookuptable_1_out[4]), .Dout(Dout));
  Memory_Cell memory_cell_2 (
    .ld(ld), .Din(Din), .str(str), .row(lookuptable_1_out[1]), .column(lookuptable_1_out[4]), .Dout(Dout));
  Memory_Cell memory_cell_3 (
    .ld(ld), .Din(Din), .str(str), .row(lookuptable_1_out[2]), .column(lookuptable_1_out[4]), .Dout(Dout));
  Memory_Cell memory_cell_4 (
    .ld(ld), .Din(Din), .str(str), .row(lookuptable_1_out[3]), .column(lookuptable_1_out[4]), .Dout(Dout));
  Memory_Cell memory_cell_5 (
    .ld(ld), .Din(Din), .str(str), .row(lookuptable_1_out[0]), .column(lookuptable_1_out[5]), .Dout(Dout));
  Memory_Cell memory_cell_6 (
    .ld(ld), .Din(Din), .str(str), .row(lookuptable_1_out[1]), .column(lookuptable_1_out[5]), .Dout(Dout));
  Memory_Cell memory_cell_7 (
    .ld(ld), .Din(Din), .str(str), .row(lookuptable_1_out[2]), .column(lookuptable_1_out[5]), .Dout(Dout));
  Memory_Cell memory_cell_8 (
    .ld(ld), .Din(Din), .str(str), .row(lookuptable_1_out[3]), .column(lookuptable_1_out[5]), .Dout(Dout));
  Memory_Cell memory_cell_9 (
    .ld(ld), .Din(Din), .str(str), .row(lookuptable_1_out[0]), .column(lookuptable_1_out[6]), .Dout(Dout));
  Memory_Cell memory_cell_10 (
    .ld(ld), .Din(Din), .str(str), .row(lookuptable_1_out[1]), .column(lookuptable_1_out[6]), .Dout(Dout));
  Memory_Cell memory_cell_11 (
    .ld(ld), .Din(Din), .str(str), .row(lookuptable_1_out[2]), .column(lookuptable_1_out[6]), .Dout(Dout));
  Memory_Cell memory_cell_12 (
    .ld(ld), .Din(Din), .str(str), .row(lookuptable_1_out[3]), .column(lookuptable_1_out[6]), .Dout(Dout));
  Memory_Cell memory_cell_13 (
    .ld(ld), .Din(Din), .str(str), .row(lookuptable_1_out[0]), .column(lookuptable_1_out[7]), .Dout(Dout));
  Memory_Cell memory_cell_14 (
    .ld(ld), .Din(Din), .str(str), .row(lookuptable_1_out[1]), .column(lookuptable_1_out[7]), .Dout(Dout));
  Memory_Cell memory_cell_15 (
    .ld(ld), .Din(Din), .str(str), .row(lookuptable_1_out[2]), .column(lookuptable_1_out[7]), .Dout(Dout));
  Memory_Cell memory_cell_16 (
    .ld(ld), .Din(Din), .str(str), .row(lookuptable_1_out[3]), .column(lookuptable_1_out[7]), .Dout(Dout));

  // Notes on the sheet:
  //   Address_Number: 内存地址:内存单元格二位矩阵位置:查找表对应位数     
  //   0X0: 0,0 : 0001 0001
  //   0X1: 0,1 : 0010 0001
  //   0X2: 0,2 : 0100 0001
  //   0X3: 0,3 : 1000 0001
  //   0X4: 1,0 : 0001 0010
  //   0X5: 1,1 : 0010 0010
  //   0X6: 1,2 : 0100 0010
  //   0X7: 1,3 : 1000 0010
  //   0X8: 2,0 : 0001 0100
  //   0X9: 2,1 : 0010 0100
  //   0XA: 2,2 : 0100 0100
  //   0XB: 2,3 : 1000 0100
  //   0XC: 3,0 : 0001 1000
  //   0XD: 3,1 : 0010 1000
  //   0XE: 3,2 : 0100 1000
  //   0XF: 3,3 : 1000 1000
  //   contents of lookuptable_1 (hex, n*v repeats v):
  //   11,21,41,81,12,22,42,82,14,24,44,84,18,28,48,88
endmodule
