// Digital circuit Memory_Cell.dig as structural Verilog
module Memory_Cell (
  input  ld,
  input  Din,
  input  str,
  input  row,
  input  column,
  output Dout
);

  wire and_1_out, and_2_out, and_3_out, latch_1_p3;

  and and_1 (and_1_out, row, column);
  and and_2 (and_2_out, ld, and_1_out);
  and and_3 (and_3_out, str, and_1_out);
  // Latch latch_1: pin names not known; wires that end beside it: Din, and_3_out, latch_1_p3
  assign Dout = and_2_out ? latch_1_p3 : 1'bz;  // Driver driver_1
  PullDown pulldown_1 (.out(Dout));
endmodule
