// Digital circuit NOT.dig as structural Verilog
module NOT (
  input  in_2,
  output out_1
);

  // RelayDT relaydt_1: pin names not known; wires that end beside it: in_2, 1'b1, 1'b0, out_1
  PullDown pulldown_1 (.out(out_1));
endmodule
