// Digital circuit Edge_triggered_Flip_flop_Latch.dig as structural Verilog
module Edge_triggered_Flip_flop_Latch (
  input  Din,
  output Dout
);

  wire Clock_out, latch_1_p3, not_1_out;

  Button Clock (.out(Clock_out));
  not not_1 (not_1_out, Clock_out);
  // Latch latch_1: pin names not known; wires that end beside it: Din, Clock_out, latch_1_p3
  // Latch latch_2: pin names not known; wires that end beside it: latch_1_p3, not_1_out, Dout
endmodule
