// Digital circuit SysRegister.dig as structural Verilog
module SysRegister (
  input  [7:0] in_2,
  input  in_3,
  output [7:0] out_1
);

  wire button_1_out;

  Button button_1 (.out(button_1_out));
  Register #(.Bits(8)) register_1 (.D(in_2), .C(button_1_out), .en(in_3), .Q(out_1));
endmodule
