// Digital circuit SysRegister_OutEnable.dig as structural Verilog
module SysRegister_OutEnable (
  input  [1:0] Din,
  input  EN,
  input  OE,
  output out_2,
  output out_5
);

  wire Clock_out;
  wire [1:0] register_1_q;

  Button Clock (.out(Clock_out));
  Register #(.Bits(2)) register_1 (.D(Din), .C(Clock_out), .en(EN), .Q(register_1_q));
  // RelayDT relaydt_1: pin names not known; wires that end beside it: OE, register_1_q[0], OE, 1'b0, out_2, 1'b0
  // RelayDT relaydt_2: pin names not known; wires that end beside it: register_1_q[1], out_5
  PullDown pulldown_1 (.out(out_2));
  PullDown pulldown_2 (.out(out_5));
endmodule
