// Digital circuit SysRegister_Drive.dig as structural Verilog
module SysRegister_Drive (
  input  [1:0] Din,
  input  EN,
  input  OE,
  output [1:0] out_4
);

  wire Clock_out;
  wire [1:0] register_1_q;

  Button Clock (.out(Clock_out));
  Register #(.Bits(2)) register_1 (.D(Din), .C(Clock_out), .en(EN), .Q(register_1_q));
  assign out_4 = OE ? register_1_q : 2'bz;  // Driver driver_1
endmodule
