// Digital circuit XOR_with_and_or_not.dig as structural Verilog
module XOR_with_and_or_not (
  input  in_2,
  input  in_3,
  output out_1
);

  wire and_1_out, not_1_out, or_1_out;

  and and_1 (and_1_out, in_2, in_3);
  or or_1 (or_1_out, in_2, in_3);
  not not_1 (not_1_out, and_1_out);
  and and_2 (out_1, not_1_out, or_1_out);
endmodule
